// Logisim project CRC.circ as structural Verilog: 2 circuits, main circuit CRC
module _4_4 (
  input  [3:0] \被除数 ,
  input  [3:0] \除数 ,
  output \商 ,
  output [2:0] out_4
);

  wire comparator_1_eq, not_1_out;
  wire [3:0] xor_1_out;
  wire [3:3] multiplexer_2_out;

  Comparator #(.width(1)) comparator_1 (.a(\被除数 [3]), .b(1'b1), .eq(comparator_1_eq));  // open: gt, lt
  assign xor_1_out = \被除数  ^ \除数 ;  // XOR_Gate xor_1, 4 bits wide
  not not_1 (not_1_out, comparator_1_eq);
  Multiplexer multiplexer_1 (.in0(1'b1), .in1(1'b0), .out(\商 ), .sel(not_1_out));  // open: en
  Multiplexer #(.width(4)) multiplexer_2 (
    .in0(xor_1_out), .in1(\被除数 ), .out({multiplexer_2_out[3], out_4}), .sel(not_1_out));  // open: en

  // Notes on the sheet:
  //   余数
endmodule

module CRC (
  input  [7:0] in_1,
  input  [3:0] in_2,
  output [10:0] out_3
);

  wire \n4_4_1_商 , \n4_4_2_商 , \n4_4_3_商 , \n4_4_4_商 , \n4_4_5_商 , \n4_4_6_商 , \n4_4_7_商 ;
  wire [2:0] n4_4_1_out_4, n4_4_2_out_4, n4_4_3_out_4, n4_4_4_out_4, n4_4_5_out_4, n4_4_6_out_4, n4_4_7_out_4;

  _4_4 u_4_4_1 (.\被除数 (in_1[7:4]), .\除数 (in_2), .\商 (\n4_4_1_商 ), .out_4(n4_4_1_out_4));
  _4_4 u_4_4_2 (.\被除数 ({n4_4_1_out_4, in_1[3]}), .\除数 (in_2), .\商 (\n4_4_2_商 ), .out_4(n4_4_2_out_4));
  _4_4 u_4_4_3 (.\被除数 ({n4_4_2_out_4, in_1[2]}), .\除数 (in_2), .\商 (\n4_4_3_商 ), .out_4(n4_4_3_out_4));
  _4_4 u_4_4_4 (.\被除数 ({n4_4_3_out_4, in_1[1]}), .\除数 (in_2), .\商 (\n4_4_4_商 ), .out_4(n4_4_4_out_4));
  _4_4 u_4_4_5 (.\被除数 ({n4_4_4_out_4, in_1[0]}), .\除数 (in_2), .\商 (\n4_4_5_商 ), .out_4(n4_4_5_out_4));
  _4_4 u_4_4_6 (.\被除数 ({n4_4_5_out_4, 1'b0}), .\除数 (in_2), .\商 (\n4_4_6_商 ), .out_4(n4_4_6_out_4));
  _4_4 u_4_4_7 (.\被除数 ({n4_4_6_out_4, 1'b0}), .\除数 (in_2), .\商 (\n4_4_7_商 ), .out_4(n4_4_7_out_4));
  _4_4 u_4_4_8 (.\被除数 ({n4_4_7_out_4, 1'b0}), .\除数 (in_2), .out_4(out_3[2:0]));  // open: 商

  assign out_3[10:3] = in_1;
endmodule
