// Logisim project P3_Project.circ as structural Verilog: 11 circuits, main circuit main
module main (
);

  wire alu_zero, ALUsrc, ExtOp, jal, LuiOp, Memread, Memtoreg, Memwrite, not_1_out, Regdst, Regwrite, reset;
  wire [1:0] ALUOp;
  wire [2:0] Npc_slc;
  wire [4:0] multiplexer_1_out, RegAddr;
  wire [5:0] Fun;
  wire [9:0] MemAddr;
  wire [15:6] imm16;
  wire [25:16] imm26;
  wire [31:0] alu_1_out_4, dm_1_out_6, ext32, grf_1_out_7, ifu_1_pc_put, \input , multiplexer_3_out,
       multiplexer_4_out, pc_1_pc_new, PC_4, Write_data;
  wire [31:26] Instr;

  Multiplexer #(.width(5)) multiplexer_1 (
    .in0(imm26[20:16]), .in1(imm16[15:11]), .out(multiplexer_1_out), .sel(Regdst));  // open: en
  IFU ifu_1 (
    .in_3(ext32), .pc_put(ifu_1_pc_put), .nPC_sel(Npc_slc), .zero(alu_zero), .in_2({imm26, imm16, Fun}),
    .pc4(PC_4), .pc_in(pc_1_pc_new));
  Multiplexer #(.width(5)) multiplexer_2 (
    .in0(multiplexer_1_out), .in1({5{1'b1}}), .out(RegAddr), .sel(jal));  // open: en
  pc pc_1 (.pc_old(ifu_1_pc_put), .reset(reset), .pc_new(pc_1_pc_new));
  GRF grf_1 (
    .Read_1(imm26[25:21]), .Read2(imm26[20:16]), .Write_register(RegAddr), .in_6(Write_data),
    .out_7(grf_1_out_7), .out_8(\input ), .reset(reset), .WE(Regwrite));
  EXT ext_1 (.in_1({imm16, Fun}), .ExOp(ExtOp), .LuiOp(LuiOp), .out_4(ext32));
  im im_1 (.address(pc_1_pc_new[11:2]), .instr({Instr, imm26, imm16, Fun}));
  Multiplexer #(.width(32)) multiplexer_3 (
    .in0(\input ), .in1(ext32), .out(multiplexer_3_out), .sel(ALUsrc));  // open: en
  ALU alu_1 (
    .in_1(grf_1_out_7), .in_2(multiplexer_3_out), .ALUOP(ALUOp),
    .out_4({alu_1_out_4[31:12], MemAddr, alu_1_out_4[1:0]}), .ALU_equ(alu_zero));
  CONTROL control_1 (
    .op(Instr), .fun(Fun), .regdst(Regdst), .ALUsrc(ALUsrc), .MemtoReg(Memtoreg), .Regwrite(Regwrite),
    .Memwrite(Memwrite), .EXTop(ExtOp), .Memread(Memread), .Luiop(LuiOp), .ALUop(ALUOp), .nPC_slc(Npc_slc),
    .jal(jal));
  DM dm_1 (.Add(MemAddr), .in_2(\input ), .Memwrite(Memwrite), .Memread(Memread), .out_6(dm_1_out_6), .reset(reset));
  not not_1 (not_1_out, Memtoreg);
  Multiplexer #(.width(32)) multiplexer_4 (
    .in0(dm_1_out_6), .in1({alu_1_out_4[31:12], MemAddr, alu_1_out_4[1:0]}), .out(multiplexer_4_out),
    .sel(not_1_out));  // open: en
  Multiplexer #(.width(32)) multiplexer_5 (
    .in0(multiplexer_4_out), .in1(PC_4), .out(Write_data), .sel(jal));  // open: en

  // Other names for the same wires on the sheet: imm16[5:0] = Fun; imm26[15:0] = {imm16, Fun};
  //   Instr[25:0] = {imm26, imm16, Fun}; Shamt[4:0] = imm16[10:6]; Rd[4:0] = imm16[15:11]; Op[5:0] = Instr;
  //   Rs[4:0] = imm26[25:21]; Rt[4:0] = imm26[20:16]

  // Notes on the sheet:
  //   每条加的指令分成不同电路图
  //   每加一次，改变“所有”控制信号，是否改变GRF\PC\DM\IM的输出输入(通过新的if控制信号选择mux)
endmodule

module ALU (
  input  [31:0] in_1,
  input  [31:0] in_2,
  input  [1:0] ALUOP,
  output [31:0] out_4,
  output ALU_equ
);

  wire [31:0] adder_1_out, and_1_out, or_1_out, subtractor_1_out;

  assign and_1_out = in_1 & in_2;  // AND_Gate and_1, 32 bits wide
  assign or_1_out = in_1 | in_2;  // OR_Gate or_1, 32 bits wide
  Adder #(.width(32)) adder_1 (.a(in_1), .b(in_2), .out(adder_1_out));  // open: cin, cout
  Subtractor #(.width(32)) subtractor_1 (.a(in_1), .b(in_2), .out(subtractor_1_out));  // open: bin, bout
  Comparator #(.width(32)) comparator_1 (.a(in_1), .b(in_2), .eq(ALU_equ));  // open: gt, lt
  Multiplexer #(.select(2), .width(32)) multiplexer_1 (
    .in0(and_1_out), .in1(or_1_out), .in2(adder_1_out), .in3(subtractor_1_out), .out(out_4), .sel(ALUOP));  // open: en

  // Notes on the sheet:
  //   ALU_input1
  //   ALU_input2
  //   ALU_ans
endmodule

module GRF (
  input  reset,
  input  WE,
  input  [4:0] Read_1,
  input  [4:0] Read2,
  input  [4:0] Write_register,
  input  [31:0] in_6,
  output [31:0] out_7,
  output [31:0] out_8
);

  wire _0, c1, c2, c3, c4, c5, c6, c7, c8, c9, c10, c11, c12, c13, c14, c15, c16, c17, c18, c19, c20, c21,
       c22, c23, c24, c25, c26, c27, c28, c29, c30, c31, c32;
  wire [31:0] a1, a2, a3, a4, a5, a6, a7, a8, a9, a10, a11, a12, a13, a14, a15, a16, a17, a18, a19, a20, a21,
       a22, a23, a24, a25, a26, a27, a28, a29, a30, a31, a32, b1, b2, b3, b4, b5, b6, b7, b8, b9, b10, b11,
       b12, b13, b14, b15, b16, b17, b18, b19, b20, b21, b22, b23, b24, b25, b26, b27, b28, b29, b30, b31,
       b32;

  Clock clock_1 (.out(_0));
  Demultiplexer #(.select(5), .width(32)) demultiplexer_1 (
    .out0(a1), .out1(a2), .out2(a3), .out3(a4), .out4(a5), .out5(a6), .out6(a7), .out7(a8), .out8(a9),
    .out9(a10), .out10(a11), .out11(a12), .out12(a13), .out13(a14), .out14(a15), .out15(a16), .out16(a17),
    .out17(a18), .out18(a19), .out19(a20), .out20(a21), .out21(a22), .out22(a23), .out23(a24), .out24(a25),
    .out25(a26), .out26(a27), .out27(a28), .out28(a29), .out29(a30), .out30(a31), .out31(a32), .in(in_6),
    .sel(Write_register));  // open: en
  Demultiplexer #(.select(5)) demultiplexer_2 (
    .out0(c1), .out1(c2), .out2(c3), .out3(c4), .out4(c5), .out5(c6), .out6(c7), .out7(c8), .out8(c9),
    .out9(c10), .out10(c11), .out11(c12), .out12(c13), .out13(c14), .out14(c15), .out15(c16), .out16(c17),
    .out17(c18), .out18(c19), .out19(c20), .out20(c21), .out21(c22), .out22(c23), .out23(c24), .out24(c25),
    .out25(c26), .out26(c27), .out27(c28), .out28(c29), .out29(c30), .out30(c31), .out31(c32), .in(WE),
    .sel(Write_register));  // open: en
  // Probe on {32{1'b0}}
  // Probe on {32{1'b0}}
  Multiplexer #(.select(5), .width(32)) multiplexer_1 (
    .in0({32{1'b0}}), .in1(b2), .in2(b3), .in3(b4), .in4(b5), .in5(b6), .in6(b7), .in7(b8), .in8(b9),
    .in9(b10), .in10(b11), .in11(b12), .in12(b13), .in13(b14), .in14(b15), .in15(b16), .in16(b17),
    .in17(b18), .in18(b19), .in19(b20), .in20(b21), .in21(b22), .in22(b23), .in23(b24), .in24(b25),
    .in25(b26), .in26(b27), .in27(b28), .in28(b29), .in29(b30), .in30(b31), .in31(b32), .out(out_7),
    .sel(Read_1));  // open: en
  Multiplexer #(.select(5), .width(32)) multiplexer_2 (
    .in0({32{1'b0}}), .in1(b2), .in2(b3), .in3(b4), .in4(b5), .in5(b6), .in6(b7), .in7(b8), .in8(b9),
    .in9(b10), .in10(b11), .in11(b12), .in12(b13), .in13(b14), .in14(b15), .in15(b16), .in16(b17),
    .in17(b18), .in18(b19), .in19(b20), .in20(b21), .in21(b22), .in22(b23), .in23(b24), .in24(b25),
    .in25(b26), .in26(b27), .in27(b28), .in28(b29), .in29(b30), .in30(b31), .in31(b32), .out(out_8),
    .sel(Read2));  // open: en
  Register #(.width(32)) register_1 (.D(a1), .en(1'b0), .Q(b1), .clk(_0), .clr(reset));
  Register #(.width(32)) register_2 (.D(a9), .en(c9), .Q(b9), .clk(_0), .clr(reset));
  Register #(.width(32)) register_3 (.D(a17), .en(c17), .Q(b17), .clk(_0), .clr(reset));
  Register #(.width(32)) register_4 (.D(a25), .en(c25), .Q(b25), .clk(_0), .clr(reset));
  Register #(.width(32)) register_5 (.D(a2), .en(c2), .Q(b2), .clk(_0), .clr(reset));
  Register #(.width(32)) register_6 (.D(a10), .en(c10), .Q(b10), .clk(_0), .clr(reset));
  Register #(.width(32)) register_7 (.D(a18), .en(c18), .Q(b18), .clk(_0), .clr(reset));
  Register #(.width(32)) register_8 (.D(a26), .en(c26), .Q(b26), .clk(_0), .clr(reset));
  Register #(.width(32)) register_9 (.D(a3), .en(c3), .Q(b3), .clk(_0), .clr(reset));
  Register #(.width(32)) register_10 (.D(a11), .en(c11), .Q(b11), .clk(_0), .clr(reset));
  Register #(.width(32)) register_11 (.D(a19), .en(c19), .Q(b19), .clk(_0), .clr(reset));
  Register #(.width(32)) register_12 (.D(a27), .en(c27), .Q(b27), .clk(_0), .clr(reset));
  Register #(.width(32)) register_13 (.D(a4), .en(c4), .Q(b4), .clk(_0), .clr(reset));
  Register #(.width(32)) register_14 (.D(a12), .en(c12), .Q(b12), .clk(_0), .clr(reset));
  Register #(.width(32)) register_15 (.D(a20), .en(c20), .Q(b20), .clk(_0), .clr(reset));
  Register #(.width(32)) register_16 (.D(a28), .en(c28), .Q(b28), .clk(_0), .clr(reset));
  Register #(.width(32)) register_17 (.D(a5), .en(c5), .Q(b5), .clk(_0), .clr(reset));
  Register #(.width(32)) register_18 (.D(a13), .en(c13), .Q(b13), .clk(_0), .clr(reset));
  Register #(.width(32)) register_19 (.D(a21), .en(c21), .Q(b21), .clk(_0), .clr(reset));
  Register #(.width(32)) register_20 (.D(a29), .en(c29), .Q(b29), .clk(_0), .clr(reset));
  Register #(.width(32)) register_21 (.D(a6), .en(c6), .Q(b6), .clk(_0), .clr(reset));
  Register #(.width(32)) register_22 (.D(a14), .en(c14), .Q(b14), .clk(_0), .clr(reset));
  Register #(.width(32)) register_23 (.D(a22), .en(c22), .Q(b22), .clk(_0), .clr(reset));
  Register #(.width(32)) register_24 (.D(a30), .en(c30), .Q(b30), .clk(_0), .clr(reset));
  Register #(.width(32)) register_25 (.D(a7), .en(c7), .Q(b7), .clk(_0), .clr(reset));
  Register #(.width(32)) register_26 (.D(a15), .en(c15), .Q(b15), .clk(_0), .clr(reset));
  Register #(.width(32)) register_27 (.D(a23), .en(c23), .Q(b23), .clk(_0), .clr(reset));
  Register #(.width(32)) register_28 (.D(a31), .en(c31), .Q(b31), .clk(_0), .clr(reset));
  Register #(.width(32)) register_29 (.D(a8), .en(c8), .Q(b8), .clk(_0), .clr(reset));
  Register #(.width(32)) register_30 (.D(a16), .en(c16), .Q(b16), .clk(_0), .clr(reset));
  Register #(.width(32)) register_31 (.D(a24), .en(c24), .Q(b24), .clk(_0), .clr(reset));
  Register #(.width(32)) register_32 (.D(a32), .en(c32), .Q(b32), .clk(_0), .clr(reset));

  // Other names for the same wires on the sheet: _1 = reset; _2 = WE; gg[4:0] = Read2; hh[4:0] = Read_1

  // Notes on the sheet:
  //   clk
  //   Write data
  //   !!!register-a1 here refers to $0
endmodule

module EXT (
  input  [15:0] in_1,
  input  ExOp,
  input  LuiOp,
  output [31:0] out_4
);

  wire [31:0] bit_extender_1_out, bit_extender_2_out, multiplexer_1_out;

  assign bit_extender_1_out = {{16{1'b0}}, in_1};  // Bit_Extender bit_extender_1
  assign bit_extender_2_out = {{16{in_1[15]}}, in_1};  // Bit_Extender bit_extender_2
  Multiplexer #(.width(32)) multiplexer_1 (
    .in0(bit_extender_1_out), .in1(bit_extender_2_out), .out(multiplexer_1_out), .sel(ExOp));  // open: en
  Multiplexer #(.width(32)) multiplexer_2 (
    .in0(multiplexer_1_out), .in1({in_1, {16{1'b0}}}), .out(out_4), .sel(LuiOp));  // open: en

  // Notes on the sheet:
  //   imm16
  //   ex32
endmodule

module NADD (
  input  [31:0] in_1,
  input  [31:0] in_2,
  output [31:0] out_3
);

  Adder #(.width(32)) adder_1 (.a(in_1), .b(in_2), .out(out_3));  // open: cin, cout

  // Notes on the sheet:
  //   PC+4
  //   Imm32<<2
  //   ANS
endmodule

module IFU (
  input  [2:0] nPC_sel,
  input  [25:0] in_2,
  input  [31:0] in_3,
  input  zero,
  input  [31:0] pc_in,
  output [31:0] pc_put,
  output [31:0] pc4
);

  wire [31:0] adder_1_out, beq, shifter_1_out;

  add_4 add_4_1 (.in_1(pc_in), .out_2(pc4));
  Shifter #(.width(32)) shifter_1 (.in(in_3), .\dist (5'b00010), .out(shifter_1_out));
  Adder #(.width(32)) adder_1 (.a(shifter_1_out), .b(pc4), .out(adder_1_out));  // open: cin, cout
  Multiplexer #(.width(32)) multiplexer_1 (.in0(pc4), .in1(adder_1_out), .out(beq), .sel(zero));  // open: en
  Multiplexer #(.select(3), .width(32)) multiplexer_2 (
    .in0(pc4), .in1(beq), .in2({pc_in[31:28], in_2, 2'b00}), .in3({pc_in[31:28], in_2, 2'b00}), .out(pc_put),
    .sel(nPC_sel));  // open: in4, in5, in6, in7, en

  // Other names for the same wires on the sheet: j[31:2] = {pc_in[31:28], in_2}; jal[31:2] = {pc_in[31:28], in_2}

  // Notes on the sheet:
  //   imm16
  //   offset
  //   !!!!"00->01->10->11->100->101"
endmodule

module CONTROL (
  input  [5:0] op,
  input  [5:0] fun,
  output regdst,
  output jal,
  output ALUsrc,
  output MemtoReg,
  output Regwrite,
  output Memwrite,
  output Memread,
  output EXTop,
  output Luiop,
  output [1:0] ALUop,
  output [2:0] nPC_slc
);

  wire addu, beq, j, not_1_out, not_2_out, not_3_out, not_4_out, not_5_out, not_6_out, not_7_out, not_8_out,
       not_9_out, not_10_out, not_11_out, not_12_out, not_13_out, not_14_out, not_15_out, not_16_out,
       not_17_out, not_18_out, not_19_out, not_20_out, not_21_out, not_22_out, not_23_out, not_24_out,
       not_25_out, not_26_out, not_27_out, not_28_out, not_29_out, not_30_out, not_31_out, not_32_out,
       not_33_out, not_34_out, not_35_out, not_36_out, not_37_out, not_38_out, not_39_out, not_40_out,
       not_41_out, not_42_out, not_43_out, ori, subu;

  not not_1 (not_1_out, op[0]);
  not not_2 (not_2_out, op[1]);
  not not_3 (not_3_out, op[2]);
  not not_4 (not_4_out, op[3]);
  not not_5 (not_5_out, op[4]);
  not not_6 (not_6_out, op[5]);
  not not_7 (not_7_out, fun[1]);
  not not_8 (not_8_out, fun[2]);
  not not_9 (not_9_out, fun[3]);
  not not_10 (not_10_out, fun[4]);
  not not_11 (not_11_out, op[0]);
  not not_12 (not_12_out, op[1]);
  not not_13 (not_13_out, op[2]);
  not not_14 (not_14_out, op[3]);
  not not_15 (not_15_out, op[4]);
  not not_16 (not_16_out, op[5]);
  not not_17 (not_17_out, fun[2]);
  not not_18 (not_18_out, fun[3]);
  not not_19 (not_19_out, fun[4]);
  not not_20 (not_20_out, op[1]);
  not not_21 (not_21_out, op[4]);
  not not_22 (not_22_out, op[5]);
  not not_23 (not_23_out, op[2]);
  not not_24 (not_24_out, op[3]);
  not not_25 (not_25_out, op[4]);
  not not_26 (not_26_out, op[0]);
  not not_27 (not_27_out, op[2]);
  not not_28 (not_28_out, op[3]);
  not not_29 (not_29_out, op[4]);
  not not_30 (not_30_out, op[5]);
  and and_1 (addu, not_1_out, not_2_out, not_3_out, not_4_out, not_5_out, not_6_out, fun[0], not_7_out, not_8_out, not_9_out, not_10_out, fun[5]);
  and and_2 (subu, not_11_out, not_12_out, not_13_out, not_14_out, not_15_out, not_16_out, fun[0], fun[1], not_17_out, not_18_out, not_19_out, fun[5]);
  and and_3 (ori, op[0], not_20_out, op[2], op[3], not_21_out, not_22_out);
  and and_4 (Memread, op[0], op[1], not_23_out, not_24_out, not_25_out, op[5]);
  and and_5 (j, not_26_out, op[1], not_27_out, not_28_out, not_29_out, not_30_out);
  not not_31 (not_31_out, op[2]);
  not not_32 (not_32_out, op[4]);
  not not_33 (not_33_out, op[0]);
  not not_34 (not_34_out, op[1]);
  not not_35 (not_35_out, op[3]);
  not not_36 (not_36_out, op[4]);
  not not_37 (not_37_out, op[5]);
  not not_38 (not_38_out, op[4]);
  not not_39 (not_39_out, op[5]);
  not not_40 (not_40_out, op[2]);
  not not_41 (not_41_out, op[3]);
  not not_42 (not_42_out, op[4]);
  not not_43 (not_43_out, op[5]);
  and and_6 (beq, not_33_out, not_34_out, op[2], not_35_out, not_36_out, not_37_out);
  and and_7 (Luiop, op[0], op[1], op[2], op[3], not_38_out, not_39_out);
  and and_8 (jal, op[0], op[1], not_40_out, not_41_out, not_42_out, not_43_out);
  and and_9 (Memwrite, op[0], op[1], not_31_out, op[3], not_32_out, op[5]);
  or or_1 (regdst, addu, subu);
  or or_2 (ALUsrc, ori, Memread, Memwrite, Luiop);
  or or_3 (Regwrite, addu, jal, subu, Memread, Luiop, ori);
  or or_4 (EXTop, Memwrite, beq, Memread);
  or or_5 (ALUop[1], addu, subu, Memread, Memwrite, Luiop);
  or or_6 (ALUop[0], subu, ori);
  buf or_7 (nPC_slc[2], 1'b0);  // OR_Gate
  or or_8 (nPC_slc[1], jal, j);
  or or_9 (nPC_slc[0], jal, beq);

  assign MemtoReg = Memread;

  // Other names for the same wires on the sheet: lui = Luiop; lw = Memread; sw = Memwrite
endmodule

module DM (
  input  [9:0] Add,
  input  [31:0] in_2,
  input  Memwrite,
  input  Memread,
  input  reset,
  output [31:0] out_6
);

  wire clock_1_out;

  Clock clock_1 (.out(clock_1_out));
  RAM #(.addrWidth(10), .dataWidth(32), .bus("separate")) ram_1 (
    .addr(Add), .din(in_2), .data(out_6), .str(Memwrite), .clk(clock_1_out), .ld(Memread), .clr(reset));  // open: sel

  // Notes on the sheet:
  //   Input
  //   Output
endmodule

module add_4 (
  input  [31:0] in_1,
  output [31:0] out_2
);

  Adder #(.width(32)) adder_1 (.a(in_1), .b(32'h4), .out(out_2));  // open: cin, cout
endmodule

module im (
  input  [9:0] address,
  output [31:0] instr
);

  ROM #(.addrWidth(10), .dataWidth(32)) rom_1 (.addr(address), .data(instr));  // open: sel

  // Notes on the sheet:
  //   contents of rom_1 (hex, n*v repeats v):
  //   35080001 1084021 c000c01
  //   out
endmodule

module pc (
  input  [31:0] pc_old,
  input  reset,
  output [31:0] pc_new
);

  wire clock_1_out;

  Clock clock_1 (.out(clock_1_out));
  Register #(.width(32)) register_1 (.D(pc_old), .Q(pc_new), .clk(clock_1_out), .clr(reset));  // open: en
endmodule
