// Logisim project fsm.circ as structural Verilog: 4 circuits, main circuit fsm
module fsm (
  input  [1:0] \input ,
  input  CLR,
  output out_3
);

  wire [1:0] change_mode_1_out_4, output_1_acient_mode_2, save_mode_1_out_2;

  change_mode change_mode_1 (
    .\input (\input ), .acient_condition(output_1_acient_mode_2), .CLR(CLR), .out_4(change_mode_1_out_4));
  save_mode save_mode_1 (.in_1(change_mode_1_out_4), .out_2(save_mode_1_out_2));
  \output  output_1 (
    .\input (\input ), .acient_mode(save_mode_1_out_2), .ans(out_3), .acient_mode_2(output_1_acient_mode_2));

  // Notes on the sheet:
  //   1.状态转移图
  //   2.change和output 均用真值表
  //   3.同步复位vs异步复位
  //   change
  //   save
  //   output
endmodule

module change_mode (
  input  [1:0] \input ,
  input  [1:0] acient_condition,
  input  CLR,
  output [1:0] out_4
);

  wire and_1_out, and_2_out, and_3_out, and_4_out, not_1_out, not_2_out, not_3_out, not_4_out, not_5_out,
       not_6_out, not_7_out, not_8_out, not_9_out, not_10_out, not_11_out;

  not not_1 (not_1_out, acient_condition[1]);
  not not_2 (not_2_out, \input [0]);
  not not_3 (not_3_out, CLR);
  not not_4 (not_4_out, acient_condition[0]);
  not not_5 (not_5_out, \input [0]);
  not not_6 (not_6_out, CLR);
  not not_7 (not_7_out, \input [1]);
  not not_8 (not_8_out, CLR);
  not not_9 (not_9_out, acient_condition[0]);
  not not_10 (not_10_out, \input [0]);
  not not_11 (not_11_out, CLR);
  and and_1 (and_1_out, not_1_out, acient_condition[0], not_2_out, not_3_out);
  and and_2 (and_2_out, acient_condition[1], not_4_out, not_5_out, not_6_out);
  and and_3 (and_3_out, not_7_out, \input [0], not_8_out);
  and and_4 (and_4_out, acient_condition[1], not_9_out, not_10_out, not_11_out);
  or or_1 (out_4[1], and_1_out, and_2_out);
  or or_2 (out_4[0], and_3_out, and_4_out);
endmodule

module save_mode (
  input  [1:0] in_1,
  output [1:0] out_2
);

  wire clock_1_out;

  Clock clock_1 (.out(clock_1_out));
  Register #(.width(2)) register_1 (.D(in_1), .Q(out_2), .clk(clock_1_out));  // open: en, clr
endmodule

module \output  (
  input  [1:0] \input ,
  input  [1:0] acient_mode,
  output ans,
  output [1:0] acient_mode_2
);

  wire not_1_out, not_2_out;

  not not_1 (not_1_out, \input [0]);
  not not_2 (not_2_out, acient_mode[0]);
  and and_1 (ans, not_1_out, acient_mode[1], not_2_out);

  assign acient_mode_2 = acient_mode;
endmodule
