// Logisim project grf.circ as structural Verilog: 1 circuit, main circuit grf
module grf (
  input  clk,
  input  reset,
  input  WE,
  input  [4:0] A1,
  input  [4:0] A2,
  input  [4:0] A3,
  input  [31:0] in_7,
  output [31:0] out_8,
  output [31:0] out_9
);

  wire c1, c2, c3, c4, c5, c6, c7, c8, c9, c10, c11, c12, c13, c14, c15, c16, c17, c18, c19, c20, c21, c22,
       c23, c24, c25, c26, c27, c28, c29, c30, c31, c32;
  wire [31:0] a1_t, a2_t, a3_t, a4, a5, a6, a7, a8, a9, a10, a11, a12, a13, a14, a15, a16, a17, a18, a19,
       a20, a21, a22, a23, a24, a25, a26, a27, a28, a29, a30, a31, a32, b1, b2, b3, b4, b5, b6, b7, b8, b9,
       b10, b11, b12, b13, b14, b15, b16, b17, b18, b19, b20, b21, b22, b23, b24, b25, b26, b27, b28, b29,
       b30, b31, b32;

  Demultiplexer #(.select(5), .width(32)) demultiplexer_1 (
    .out0(a1_t), .out1(a2_t), .out2(a3_t), .out3(a4), .out4(a5), .out5(a6), .out6(a7), .out7(a8), .out8(a9),
    .out9(a10), .out10(a11), .out11(a12), .out12(a13), .out13(a14), .out14(a15), .out15(a16), .out16(a17),
    .out17(a18), .out18(a19), .out19(a20), .out20(a21), .out21(a22), .out22(a23), .out23(a24), .out24(a25),
    .out25(a26), .out26(a27), .out27(a28), .out28(a29), .out29(a30), .out30(a31), .out31(a32), .in(in_7),
    .sel(A3));  // open: en
  Demultiplexer #(.select(5)) demultiplexer_2 (
    .out0(c1), .out1(c2), .out2(c3), .out3(c4), .out4(c5), .out5(c6), .out6(c7), .out7(c8), .out8(c9),
    .out9(c10), .out10(c11), .out11(c12), .out12(c13), .out13(c14), .out14(c15), .out15(c16), .out16(c17),
    .out17(c18), .out18(c19), .out19(c20), .out20(c21), .out21(c22), .out22(c23), .out23(c24), .out24(c25),
    .out25(c26), .out26(c27), .out27(c28), .out28(c29), .out29(c30), .out30(c31), .out31(c32), .in(WE),
    .sel(A3));  // open: en
  // Probe on {32{1'b0}}
  // Probe on {32{1'b0}}
  Multiplexer #(.select(5), .width(32)) multiplexer_1 (
    .in0({32{1'b0}}), .in1(b2), .in2(b3), .in3(b4), .in4(b5), .in5(b6), .in6(b7), .in7(b8), .in8(b9),
    .in9(b10), .in10(b11), .in11(b12), .in12(b13), .in13(b14), .in14(b15), .in15(b16), .in16(b17),
    .in17(b18), .in18(b19), .in19(b20), .in20(b21), .in21(b22), .in22(b23), .in23(b24), .in24(b25),
    .in25(b26), .in26(b27), .in27(b28), .in28(b29), .in29(b30), .in30(b31), .in31(b32), .out(out_8), .sel(A1));  // open: en
  Multiplexer #(.select(5), .width(32)) multiplexer_2 (
    .in0({32{1'b0}}), .in1(b2), .in2(b3), .in3(b4), .in4(b5), .in5(b6), .in6(b7), .in7(b8), .in8(b9),
    .in9(b10), .in10(b11), .in11(b12), .in12(b13), .in13(b14), .in14(b15), .in15(b16), .in16(b17),
    .in17(b18), .in18(b19), .in19(b20), .in20(b21), .in21(b22), .in22(b23), .in23(b24), .in24(b25),
    .in25(b26), .in26(b27), .in27(b28), .in28(b29), .in29(b30), .in30(b31), .in31(b32), .out(out_9), .sel(A2));  // open: en
  Register #(.width(32)) register_1 (.D(a1_t), .en(1'b0), .Q(b1), .clk(clk), .clr(reset));
  Register #(.width(32)) register_2 (.D(a9), .en(c9), .Q(b9), .clk(clk), .clr(reset));
  Register #(.width(32)) register_3 (.D(a17), .en(c17), .Q(b17), .clk(clk), .clr(reset));
  Register #(.width(32)) register_4 (.D(a25), .en(c25), .Q(b25), .clk(clk), .clr(reset));
  Register #(.width(32)) register_5 (.D(a2_t), .en(c2), .Q(b2), .clk(clk), .clr(reset));
  Register #(.width(32)) register_6 (.D(a10), .en(c10), .Q(b10), .clk(clk), .clr(reset));
  Register #(.width(32)) register_7 (.D(a18), .en(c18), .Q(b18), .clk(clk), .clr(reset));
  Register #(.width(32)) register_8 (.D(a26), .en(c26), .Q(b26), .clk(clk), .clr(reset));
  Register #(.width(32)) register_9 (.D(a3_t), .en(c3), .Q(b3), .clk(clk), .clr(reset));
  Register #(.width(32)) register_10 (.D(a11), .en(c11), .Q(b11), .clk(clk), .clr(reset));
  Register #(.width(32)) register_11 (.D(a19), .en(c19), .Q(b19), .clk(clk), .clr(reset));
  Register #(.width(32)) register_12 (.D(a27), .en(c27), .Q(b27), .clk(clk), .clr(reset));
  Register #(.width(32)) register_13 (.D(a4), .en(c4), .Q(b4), .clk(clk), .clr(reset));
  Register #(.width(32)) register_14 (.D(a12), .en(c12), .Q(b12), .clk(clk), .clr(reset));
  Register #(.width(32)) register_15 (.D(a20), .en(c20), .Q(b20), .clk(clk), .clr(reset));
  Register #(.width(32)) register_16 (.D(a28), .en(c28), .Q(b28), .clk(clk), .clr(reset));
  Register #(.width(32)) register_17 (.D(a5), .en(c5), .Q(b5), .clk(clk), .clr(reset));
  Register #(.width(32)) register_18 (.D(a13), .en(c13), .Q(b13), .clk(clk), .clr(reset));
  Register #(.width(32)) register_19 (.D(a21), .en(c21), .Q(b21), .clk(clk), .clr(reset));
  Register #(.width(32)) register_20 (.D(a29), .en(c29), .Q(b29), .clk(clk), .clr(reset));
  Register #(.width(32)) register_21 (.D(a6), .en(c6), .Q(b6), .clk(clk), .clr(reset));
  Register #(.width(32)) register_22 (.D(a14), .en(c14), .Q(b14), .clk(clk), .clr(reset));
  Register #(.width(32)) register_23 (.D(a22), .en(c22), .Q(b22), .clk(clk), .clr(reset));
  Register #(.width(32)) register_24 (.D(a30), .en(c30), .Q(b30), .clk(clk), .clr(reset));
  Register #(.width(32)) register_25 (.D(a7), .en(c7), .Q(b7), .clk(clk), .clr(reset));
  Register #(.width(32)) register_26 (.D(a15), .en(c15), .Q(b15), .clk(clk), .clr(reset));
  Register #(.width(32)) register_27 (.D(a23), .en(c23), .Q(b23), .clk(clk), .clr(reset));
  Register #(.width(32)) register_28 (.D(a31), .en(c31), .Q(b31), .clk(clk), .clr(reset));
  Register #(.width(32)) register_29 (.D(a8), .en(c8), .Q(b8), .clk(clk), .clr(reset));
  Register #(.width(32)) register_30 (.D(a16), .en(c16), .Q(b16), .clk(clk), .clr(reset));
  Register #(.width(32)) register_31 (.D(a24), .en(c24), .Q(b24), .clk(clk), .clr(reset));
  Register #(.width(32)) register_32 (.D(a32), .en(c32), .Q(b32), .clk(clk), .clr(reset));

  // Other names for the same wires on the sheet: _0 = clk; _1 = reset; _2 = WE; gg[4:0] = A2; hh[4:0] = A1

  // Notes on the sheet:
  //   1.tunnel不能在不同子电路！！！
  //   2.布线不能重叠！！！
  //   4.最后的appearance 必须一毛一样
  //   3.DMX MUX 没被选择的一端会输出XXXXXX，可能会覆盖
  //   寄存器，所以此时必须让Register的En=0
  //   WD
endmodule
