// Logisim project pre.circ as structural Verilog: 3 circuits, main circuit main
module main (
  input  [2:0] in_1,
  output [3:0] out_2
);

  wire clock_1_out, comparator_1_eq;
  wire [3:0] a1_1_out_2, a2_1_out_2, adder_1_out, adder_2_out, counter_1_q;

  // Probe on a1_1_out_2
  a1 a1_1 (.in_1(a2_1_out_2), .out_2(a1_1_out_2));
  // Probe on a2_1_out_2
  a2 a2_1 (.in_1(adder_1_out), .out_2(a2_1_out_2));
  Clock clock_1 (.out(clock_1_out));
  Adder #(.width(4)) adder_1 (.a(a1_1_out_2), .b(a2_1_out_2), .out(adder_1_out));  // open: cin, cout
  Adder #(.width(4)) adder_2 (.a(4'b0010), .b({1'b0, in_1}), .out(adder_2_out));  // open: cin, cout
  Counter #(.width(4), .max('hf), .ongoal("stay")) counter_1 (
    .Q(counter_1_q), .clk(clock_1_out));  // open: load, D, count, carry, clr
  Comparator #(.width(4), .mode("unsigned")) comparator_1 (
    .a(adder_2_out), .b(counter_1_q), .eq(comparator_1_eq));  // open: gt, lt
  Register #(.width(4)) register_1 (.D(a1_1_out_2), .en(comparator_1_eq), .Q(out_2), .clk(clock_1_out));  // open: clr
endmodule

module a1 (
  input  [3:0] in_1,
  output [3:0] out_2
);

  wire clock_1_out, comparator_1_lt;
  wire [1:0] counter_1_q;
  wire [3:0] multiplexer_1_out;

  Clock clock_1 (.out(clock_1_out));
  Counter #(.width(2), .max('h3), .ongoal("stay")) counter_1 (
    .Q(counter_1_q), .clk(clock_1_out));  // open: load, D, count, carry, clr
  Comparator #(.width(2), .mode("unsigned")) comparator_1 (
    .a(2'b01), .b(counter_1_q), .lt(comparator_1_lt));  // open: gt, eq
  Multiplexer #(.width(4)) multiplexer_1 (
    .in0(4'b0000), .in1(in_1), .out(multiplexer_1_out), .sel(comparator_1_lt));  // open: en
  Register #(.width(4)) register_1 (.D(multiplexer_1_out), .Q(out_2), .clk(clock_1_out));  // open: en, clr
endmodule

module a2 (
  input  [3:0] in_1,
  output [3:0] out_2
);

  wire clock_1_out, comparator_1_lt;
  wire [1:0] counter_1_q;
  wire [3:0] multiplexer_1_out;

  Clock clock_1 (.out(clock_1_out));
  Counter #(.width(2), .max('h3), .ongoal("stay")) counter_1 (
    .Q(counter_1_q), .clk(clock_1_out));  // open: load, D, count, carry, clr
  Comparator #(.width(2), .mode("unsigned")) comparator_1 (
    .a(2'b01), .b(counter_1_q), .lt(comparator_1_lt));  // open: gt, eq
  Multiplexer #(.width(4)) multiplexer_1 (
    .in0(4'b0001), .in1(in_1), .out(multiplexer_1_out), .sel(comparator_1_lt));  // open: en
  Register #(.width(4)) register_1 (.D(multiplexer_1_out), .Q(out_2), .clk(clock_1_out));  // open: en, clr
endmodule
