// Logisim project twice-1.circ as structural Verilog: 5 circuits, main circuit fsm
module real_change (
  input  [1:0] mode,
  input  [1:0] \input ,
  input  reset,
  output [1:0] out_4
);

  wire and_1_out, and_2_out, and_3_out, and_4_out, not_1_out, not_2_out, not_3_out, not_4_out, not_5_out,
       not_6_out, not_7_out, not_8_out, not_9_out, not_10_out, not_11_out;

  not not_1 (not_1_out, mode[1]);
  not not_2 (not_2_out, \input [0]);
  not not_3 (not_3_out, reset);
  not not_4 (not_4_out, mode[0]);
  not not_5 (not_5_out, \input [0]);
  not not_6 (not_6_out, reset);
  not not_7 (not_7_out, \input [1]);
  not not_8 (not_8_out, reset);
  not not_9 (not_9_out, mode[0]);
  not not_10 (not_10_out, \input [0]);
  not not_11 (not_11_out, reset);
  and and_1 (and_1_out, not_1_out, mode[0], not_2_out, not_3_out);
  and and_2 (and_2_out, mode[1], not_4_out, not_5_out, not_6_out);
  and and_3 (and_3_out, not_7_out, \input [0], not_8_out);
  and and_4 (and_4_out, mode[1], not_9_out, not_10_out, not_11_out);
  or or_1 (out_4[1], and_1_out, and_2_out);
  or or_2 (out_4[0], and_3_out, and_4_out);
endmodule

module save (
  input  [1:0] in_1,
  input  in_2,
  output [1:0] out_3
);

  Register #(.width(2)) register_1 (.D(in_1), .Q(out_3), .clk(in_2));  // open: en, clr
endmodule

module out (
  input  [1:0] mode,
  input  [1:0] \input ,
  output ans
);

  wire not_1_out, not_2_out;

  not not_1 (not_1_out, mode[0]);
  not not_2 (not_2_out, \input [0]);
  and and_1 (ans, mode[1], not_1_out, not_2_out);
endmodule

module fsm (
  input  clr,
  input  [1:0] in_2,
  output out_3
);

  wire clock_1_out;
  wire [1:0] real_change_1_out_4, save_1_out_3;

  Clock clock_1 (.out(clock_1_out));
  real_change real_change_1 (.mode(save_1_out_3), .\input (in_2), .reset(clr), .out_4(real_change_1_out_4));
  save save_1 (.in_1(real_change_1_out_4), .in_2(clock_1_out), .out_3(save_1_out_3));
  // Probe on save_1_out_3
  out out_1 (.mode(save_1_out_3), .\input (in_2), .ans(out_3));
endmodule

module test (
  output clr,
  output out
);

  wire clock_1_out;
  wire [1:0] ram_1_data;
  wire [7:0] counter_1_q;

  Clock clock_1 (.out(clock_1_out));
  Counter counter_1 (.Q(counter_1_q), .clk(clock_1_out));  // open: load, D, count, carry, clr
  RAM #(.dataWidth(3)) ram_1 (.addr(counter_1_q), .data({clr, ram_1_data}));  // open: sel, clk, ld, clr
  // Probe on ram_1_data
  fsm fsm_1 (.clr(clr), .in_2(ram_1_data), .out_3(out));

  // Notes on the sheet:
  //   in
endmodule
